// Logisim project Full Circuit.circ as structural Verilog: 1 circuit, main circuit Full Circuit
module Full_Circuit (
);

  wire ALUsrc, CLK, Ext_Control, MemRead, MemWrite, Overflow, RegWrite, zero;
  wire [1:0] F_Id, F_If, MemToReg, RegDst;
  wire [2:0] multiplexer_1_out, Rd_Id, Rd_If, Rs_Id, Rs_If, Rt_Id, Rt_If;
  wire [3:0] ALUop, PCsrc, Shift_amount, Shift_amount_Id, Shift_amount_If;
  wire [4:0] Imm_5, Imm_5_Id, Imm_5_If, OP_Id, OP_If;
  wire [10:0] Imm_11, Imm_11_Id, Imm_11_If;
  wire [15:0] ALU_out, bit_extender_1_out, Ext_Out, Imm_11__5, ins, ins_Id, ins_If, Mem_out,
       multiplexer_2_out, multiplexer_3_out, Pc, PC_1, PC_Id, PC_If, Pc_If_t, R1, R2, R3, R4, R5, R6, R7,
       Rs_Data, Rt_Data, undriven;

  Register #(.width(16)) u_PC (.D(undriven), .en(1'b1), .Q(Pc_If_t), .clk(CLK));  // open: clr
  InstructionMemory_main main_1 (
    .PC_Address(Pc_If_t), .out_2(Rt_If), .out_3(Rs_If), .out_5(Rd_If), .out_6(F_If), .out_7(OP_If),
    .out_8(Imm_5_If), .out_10(Imm_11_If), .out_9(Shift_amount_If), .out_4(ins_If));
  Clock clock_1 (.out(CLK));
  // Probe on R1
  // Probe on Pc
  // Probe on R2
  // Probe on ins
  // Probe on R3
  // Probe on R4
  // Probe on R5
  // Probe on R6
  // Probe on R7
  Reg_If_Id reg_if_id_1 (
    .in_1(PC_If), .in_2(F_If), .in_3(Rt_If), .in_4(OP_If), .in_5(Rs_If), .in_6(Imm_5_If), .in_7(Rd_If),
    .in_8(Imm_11_If), .in_9(Shift_amount_If), .in_10(ins_If), .out_11(PC_Id), .out_12(F_Id), .out_13(Rt_Id),
    .out_14(OP_Id), .out_15(Rs_Id), .out_16(Imm_5_Id), .out_17(Rd_Id), .out_18(Imm_11_Id),
    .out_19(Shift_amount_Id), .out_20(ins_Id));
  Control_Unit control_unit_1 (
    .in_1(OP_Id), .in_2(F_Id), .out_4(ALUsrc), .out_3(ALUop), .out_5(MemRead), .out_6(MemWrite),
    .out_7(Ext_Control), .out_8(MemToReg), .out_9(RegWrite), .out_10(RegDst), .out_11(PCsrc));
  Multiplexer #(.select(2), .width(3), .enable("false")) multiplexer_1 (
    .in0(Rt_Id), .in1(Rd_Id), .in2(3'b001), .in3(3'b111), .out(multiplexer_1_out), .sel(RegDst));
  Multiplexer #(.select(2), .width(16), .enable("false")) multiplexer_2 (
    .in0(ALU_out), .in1(Mem_out), .in2(Imm_11__5), .in3(PC_1), .out(multiplexer_2_out), .sel(MemToReg));
  // Hazard_Detection_Unit hazard_detection_unit_1: pin names not known
  RegFile regfile_1 (
    .out_7(Rs_Data), .in_2(Rs_Id), .in_6(CLK), .out_8(Rt_Data), .in_3(Rt_Id), .in_5(RegWrite),
    .in_4(multiplexer_1_out), .in_1(multiplexer_2_out), .out_9(R1), .out_10(R2), .out_11(R3), .out_12(R4),
    .out_13(R5), .out_14(R6), .out_15(R7));
  Multiplexer #(.width(16), .enable("false")) multiplexer_3 (
    .in0(Rt_Data), .in1(Ext_Out), .out(multiplexer_3_out), .sel(ALUsrc));
  assign bit_extender_1_out = {{5{1'b0}}, Imm_11};  // Bit_Extender bit_extender_1
  Extender extender_1 (.in_1(Ext_Control), .in_2(Imm_5), .out_3(Ext_Out));
  Shifter #(.width(16)) shifter_1 (.in(bit_extender_1_out), .\dist (4'b0101), .out(Imm_11__5));
  ALU alu_1 (
    .in_1(ALUop), .in_2(Rs_Data), .in_3(multiplexer_3_out), .in_4(Shift_amount), .out_5(ALU_out),
    .out_6(zero), .out_7(Overflow));
  Data_Memory data_memory_1 (
    .Address(ALU_out), .Data_In(Rt_Data), .MemWrite(MemWrite), .MemRead(MemRead), .CLK(CLK),
    .Data_Out(Mem_out));
endmodule
